// Logisim project lab 10.circ as structural Verilog: 1 circuit, main circuit main
module main (
  input  [10:0] in_1
);

  wire clock_1_out, demultiplexer_1_out0, demultiplexer_1_out1, demultiplexer_1_out2, demultiplexer_1_out3,
       demultiplexer_1_out4, demultiplexer_1_out5, demultiplexer_1_out6, demultiplexer_1_out7;
  wire [7:0] adder_1_out, multiplexer_1_out, multiplexer_2_out, multiplexer_3_out, or_1_out, R0_2_q, R0_q,
       R1_2_q, R1_q, R2_2_q, R2_q, R3_2_q, R3_q, subtractor_1_out;

  Multiplexer #(.select(3), .width(8), .enable("false")) multiplexer_1 (
    .in0(R0_q), .in1(R1_q), .in2(R2_q), .in3(R3_q), .in4(R0_2_q), .in5(R1_2_q), .in6(R2_2_q), .in7(R3_2_q),
    .out(multiplexer_1_out), .sel(in_1[8:6]));
  Multiplexer #(.select(3), .width(8), .enable("false")) multiplexer_2 (
    .in0(R0_q), .in1(R1_q), .in2(R2_q), .in3(R3_q), .in4(R0_2_q), .in5(R1_2_q), .in6(R2_2_q), .in7(R3_2_q),
    .out(multiplexer_2_out), .sel(in_1[5:3]));
  Demultiplexer #(.select(3), .enable("false")) demultiplexer_1 (
    .out0(demultiplexer_1_out0), .out1(demultiplexer_1_out1), .out2(demultiplexer_1_out2),
    .out3(demultiplexer_1_out3), .out4(demultiplexer_1_out4), .out5(demultiplexer_1_out5),
    .out6(demultiplexer_1_out6), .out7(demultiplexer_1_out7), .in(1'b1), .sel(in_1[2:0]));
  Adder adder_1 (.a(multiplexer_1_out), .b(multiplexer_2_out), .out(adder_1_out));  // open: cin, cout
  Subtractor subtractor_1 (.a(multiplexer_1_out), .b(multiplexer_2_out), .out(subtractor_1_out));  // open: bin, bout
  assign or_1_out = multiplexer_1_out | multiplexer_2_out;  // OR_Gate or_1, 8 bits wide
  Multiplexer #(.select(2), .width(8), .enable("false")) multiplexer_3 (
    .in0(adder_1_out), .in1(subtractor_1_out), .in2(8'h5), .in3(or_1_out), .out(multiplexer_3_out),
    .sel(in_1[10:9]));
  Register R0 (.D(multiplexer_3_out), .en(demultiplexer_1_out0), .Q(R0_q), .clk(clock_1_out), .clr(1'b0));
  Register R1 (.D(multiplexer_3_out), .en(demultiplexer_1_out1), .Q(R1_q), .clk(clock_1_out), .clr(1'b0));
  Register R2 (.D(multiplexer_3_out), .en(demultiplexer_1_out2), .Q(R2_q), .clk(clock_1_out), .clr(1'b0));
  Register R3 (.D(multiplexer_3_out), .en(demultiplexer_1_out3), .Q(R3_q), .clk(clock_1_out), .clr(1'b0));
  Register R0_2 (.D(multiplexer_3_out), .en(demultiplexer_1_out4), .Q(R0_2_q), .clk(clock_1_out), .clr(1'b0));
  Register R1_2 (.D(multiplexer_3_out), .en(demultiplexer_1_out5), .Q(R1_2_q), .clk(clock_1_out), .clr(1'b0));
  Register R2_2 (.D(multiplexer_3_out), .en(demultiplexer_1_out6), .Q(R2_2_q), .clk(clock_1_out), .clr(1'b0));
  Register R3_2 (.D(multiplexer_3_out), .en(demultiplexer_1_out7), .Q(R3_2_q), .clk(clock_1_out), .clr(1'b0));
  Clock clock_1 (.out(clock_1_out));
endmodule
